# Fritzing sketch diagram (saved by Fritzing 0.9.2b)
breadboards: 1

parts:
  Part1 = Arduino Uno (Rev3)
  LED2 = LED - 3mm [color="Green (555nm)" package="3 mm [THT]"]
  LED3 = LED - 3mm [color="Yellow (592nm)" package="3 mm [THT]"]
  LED4 = LED - 3mm [color="Blue (430nm)" package="3 mm [THT]"]
  LED1 = LED - 3mm [color="Red (633nm)" package="3 mm [THT]"]
  S1 = Pushbutton [package="[SMD]"]
  S2 = Pushbutton [package="[SMD]"]
  S3 = Pushbutton [package="[SMD]"]
  S4 = Pushbutton [package="[SMD]"]

nets:
  N1: Part1.D8, LED1.anode
  N2: Part1.D9_PWM, S1.Pin_3, S1.Pin_4
  N3: Part1.GND, LED2.cathode, LED3.cathode, LED4.cathode, LED1.cathode, S1.Pin_1, S1.Pin_2, S2.Pin_1, S2.Pin_2, S3.Pin_1, S3.Pin_2, S4.Pin_1, S4.Pin_2
  N4: Part1.D2, LED3.anode
  N5: Part1.D3_PWM, S4.Pin_3, S4.Pin_4
  N6: Part1.D4, LED2.anode
  N7: Part1.D5_PWM, S3.Pin_3, S3.Pin_4
  N8: Part1.D6_PWM, LED4.anode
  N9: Part1.D7, S2.Pin_3, S2.Pin_4
